# Fritzing sketch Project1_sketch (saved by Fritzing 0.9.3b)
breadboards: 2

parts:
  Raspberry_Pi_1 = Raspberry Pi 3 [part_number=RPI-3-V1.2]  # not connected
  Raspberry_Pi_2 = Raspberry Pi 3 [part_number=RPI-3-V1.2]
  U1 = TCRT5000 [package=THT]
  Part1 = Adafruit DC+Stepper Motor HAT [part_number="Adafruit #2348"]
  R1 = Resistor [tolerance=±5% resistance=150 package="2512 [SMD]"]
  R2 = Resistor [tolerance=±5% resistance=4.7k package="2512 [SMD]"]
  R3 = Resistor [tolerance=±5% resistance=150 package="2512 [SMD]"]
  R4 = Resistor [tolerance=±5% resistance=150 package="2512 [SMD]"]
  R5 = Resistor [tolerance=±5% resistance=4.7k package="2512 [SMD]"]
  R6 = Resistor [tolerance=±5% resistance=4.7k package="2512 [SMD]"]
  U2 = TCRT5000 [package=THT]
  U3 = TCRT5000 [package=THT]
  M1 = DC Motor
  M2 = DC Motor
  VCC1 = 4 x AAA Battery Mount
  Part2 = Adafruit 1.44 inch TFT Breakout [part_number="Adafruit #2088"]
  CAMERA2 = TTL Serial JPEG Camera  # not connected
  IC1 = MCP3008 8-channel 10-bit ADC [part_number=MCP3008]

nets:
  3V3: Raspberry_Pi_2.3v3, Part2.VIN
  N1: Raspberry_Pi_2.GPIO10, Part2.MOSI
  N2: Raspberry_Pi_2.GPIO11, Part2.SCK
  N3: Raspberry_Pi_2.GPIO8, Part2.TFTCS
  N4: Raspberry_Pi_2.GPIO25, Part2.RESET
  N5: Raspberry_Pi_2.GPIO24, Part2.TFTDC
  GND: Raspberry_Pi_2.GND, Part2.GND
  N6: U1.Pin_1, R5.Pin_0, IC1.no_name_yet#1
  N7: U1.Pin_2, U1.Pin_3, Part1.GND, U2.Pin_2, U2.Pin_3, U3.Pin_2, U3.Pin_3, VCC1.-, IC1.no_name_yet#9, IC1.no_name_yet#14
  N8: U1.Pin_4, R4.Pin_1
  N9: Part1.M2A, M2.pin_1
  N10: Part1.M2B, M2.pin_2
  N11: Part1.M1B, M1.pin_2
  N12: Part1.M1A, M1.pin_1
  N13: Part1.VMOTOR, VCC1.+
  N14: Part1.3.3V, R1.Pin_0, R2.Pin_1, R3.Pin_0, R4.Pin_0, R5.Pin_1, R6.Pin_1, IC1.no_name_yet#15, IC1.no_name_yet#16
  N15: Part1.SPI_MOSI, IC1.no_name_yet#11
  N16: Part1.SPI_MISO, IC1.no_name_yet#12
  N17: Part1.SPI_SCLK, IC1.no_name_yet#13
  N18: Part1.SPI_CE0, IC1.no_name_yet#10
  N19: R1.Pin_1, U2.Pin_4
  N20: R2.Pin_0, U3.Pin_1, IC1.no_name_yet#2
  N21: R3.Pin_1, U3.Pin_4
  N22: R6.Pin_0, U2.Pin_1, IC1.no_name_yet#3

custom parts:
  TCRT5000: TCRT5000 optical reflective sensor
  Adafruit DC+Stepper Motor HAT: Let your robotic dreams come true with the new DC+Stepper Motor HAT from Adafruit. This Raspberry Pi add-on is perfect for any motion project as it can drive up to 4 DC or 2 Stepper motors with full PWM speed control. Since the Raspberry Pi does not have a lot of PWM pins, we use a fully-dedicated PWM driver chip onboard to both control motor direction and speed. This chip handles all the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
  Adafruit 1.44 inch TFT Breakout: This lovely little display breakout is the best way to add a small, colorful and bright display to any project. Since the display uses 4-wire SPI to communicate and has its own pixel-addressable frame buffer, it can be used with every kind of microcontroller. Even a very small one with low memory and few pins available! The 1.44" display has 128x128 color pixels. Unlike the low cost "Nokia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
  TTL Serial JPEG Camera: TTL Serial JPEG Camera with NTSC Out
